# Fritzing sketch dhtexample (saved by Fritzing 0.9.3b)
breadboards: 1

parts:
  DHT1 = DHT11 Humitidy and Temperature Sensor
  U1 = NodeMCU V1.0

nets:
  VDD: DHT1.VDD, U1.3V3
  N1: DHT1.DATA, U1.D3
  GND: DHT1.GND, U1.GND

custom parts:
  DHT11 Humitidy and Temperature Sensor: DHT11 Humidity and Temperature Sensor
  NodeMCU V1.0: ESP8266 based NodeMCU
